// Logisim project parity.circ as structural Verilog: 1 circuit, main circuit main
module main (
  input  B0,
  input  B1,
  input  B2,
  input  B3,
  output P
);

  wire xor_1_out, xor_2_out;

  xor xor_1 (xor_1_out, B0, B1);
  xor xor_2 (xor_2_out, B2, B3);
  xor xor_3 (P, xor_1_out, xor_2_out);

  // Notes on the sheet:
  //   lógica obtida por ajuda do professor Cesar Giacomini Penteado dia 11/11/24 as aprox. 21:28
endmodule
