// Logisim project ra.circ as structural Verilog: 1 circuit, main circuit main
module main (
);

  wire and_1_out, and_2_out, and_3_out, and_4_out, and_5_out, and_6_out, and_7_out, clock_1_out,
       decodiicador7seg_1_p5, decodiicador7seg_1_p6, decodiicador7seg_1_p7, decodiicador7seg_1_p8,
       decodiicador7seg_1_p9, decodiicador7seg_1_p10, decodiicador7seg_1_p11, decodiicador7seg_2_p5,
       decodiicador7seg_2_p6, decodiicador7seg_2_p7, decodiicador7seg_2_p8, decodiicador7seg_2_p9,
       decodiicador7seg_2_p10, decodiicador7seg_2_p11, decodiicador7seg_3_p5, decodiicador7seg_3_p6,
       decodiicador7seg_3_p7, decodiicador7seg_3_p8, decodiicador7seg_3_p9, decodiicador7seg_3_p10,
       decodiicador7seg_3_p11, decodiicador7seg_4_p5, decodiicador7seg_4_p6, decodiicador7seg_4_p7,
       decodiicador7seg_4_p8, decodiicador7seg_4_p9, decodiicador7seg_4_p10, decodiicador7seg_4_p11,
       decodiicador7seg_5_p5, decodiicador7seg_5_p6, decodiicador7seg_5_p7, decodiicador7seg_5_p8,
       decodiicador7seg_5_p9, decodiicador7seg_5_p10, decodiicador7seg_5_p11, decodiicador7seg_6_p5,
       decodiicador7seg_6_p6, decodiicador7seg_6_p7, decodiicador7seg_6_p8, decodiicador7seg_6_p9,
       decodiicador7seg_6_p10, decodiicador7seg_6_p11, decodiicador7seg_7_p5, decodiicador7seg_7_p6,
       decodiicador7seg_7_p7, decodiicador7seg_7_p8, decodiicador7seg_7_p9, decodiicador7seg_7_p10,
       decodiicador7seg_7_p11, main_1_p3, main_1_p4, main_1_p5, main_1_p6, main_2_p3, main_2_p4, main_2_p5,
       main_2_p6, main_3_p3, main_3_p4, main_3_p5, main_3_p6, main_4_p3, main_4_p4, main_4_p5, main_4_p6,
       main_5_p3, main_5_p4, main_5_p5, main_5_p6, main_6_p4, main_6_p5, main_6_p6, main_6_p7, main_7_p3,
       main_7_p4, main_7_p5, main_7_p6;

  and and_1 (and_1_out, main_1_p4, main_1_p3);
  Clock clock_1 (.out(clock_1_out));
  and and_2 (and_2_out, main_2_p3, main_2_p3);
  and and_3 (and_3_out, main_3_p3, main_3_p3);
  and and_4 (and_4_out, main_4_p6, main_4_p6);
  and and_5 (and_5_out, main_5_p6, main_5_p3);
  // Contador_binário_crescente_0_9_main main_1: pin names not known; wires that end beside it: clock_1_out, and_1_out, main_1_p3, main_1_p4, main_1_p5, main_1_p6
  and and_6 (and_6_out, main_6_p5, main_6_p6);
  and and_7 (and_7_out, main_7_p6, main_7_p6);
  // DECODIICADOR7SEG decodiicador7seg_1: pin names not known; wires that end beside it: main_1_p6, main_1_p5, main_1_p4, main_1_p3, decodiicador7seg_1_p5, decodiicador7seg_1_p6, decodiicador7seg_1_p7, decodiicador7seg_1_p8, decodiicador7seg_1_p9, decodiicador7seg_1_p10, decodiicador7seg_1_p11
  // Contador_binário_crescente_0_9_main main_2: pin names not known; wires that end beside it: and_1_out, and_2_out, main_2_p3, main_2_p4, main_2_p5, main_2_p6
  // Contador_binário_crescente_0_9_main main_3: pin names not known; wires that end beside it: and_2_out, and_3_out, main_3_p3, main_3_p4, main_3_p5, main_3_p6
  // Contador_binário_crescente_0_9_main main_4: pin names not known; wires that end beside it: and_3_out, and_4_out, main_4_p3, main_4_p4, main_4_p5, main_4_p6
  // Contador_binário_crescente_0_9_main main_5: pin names not known; wires that end beside it: and_4_out, and_5_out, main_5_p3, main_5_p4, main_5_p5, main_5_p6
  // Contador_binário_crescente_0_9_main main_6: pin names not known; wires that end beside it: and_6_out, and_5_out, and_6_out, main_6_p4, main_6_p5, main_6_p6, main_6_p7
  // Contador_binário_crescente_0_9_main main_7: pin names not known; wires that end beside it: and_6_out, and_7_out, main_7_p3, main_7_p4, main_7_p5, main_7_p6
  _7_Segment_Display u_7_segment_display_1 (
    .g(decodiicador7seg_1_p11), .f(decodiicador7seg_1_p10), .a(decodiicador7seg_1_p5),
    .b(decodiicador7seg_1_p6), .e(decodiicador7seg_1_p9), .d(decodiicador7seg_1_p8), .c(decodiicador7seg_1_p7));  // open: dp
  // DECODIICADOR7SEG decodiicador7seg_2: pin names not known; wires that end beside it: main_2_p6, main_2_p5, main_2_p4, main_2_p3, decodiicador7seg_2_p5, decodiicador7seg_2_p6, decodiicador7seg_2_p7, decodiicador7seg_2_p8, decodiicador7seg_2_p9, decodiicador7seg_2_p10, decodiicador7seg_2_p11
  // DECODIICADOR7SEG decodiicador7seg_3: pin names not known; wires that end beside it: main_3_p6, main_3_p5, main_3_p4, main_3_p3, decodiicador7seg_3_p5, decodiicador7seg_3_p6, decodiicador7seg_3_p7, decodiicador7seg_3_p8, decodiicador7seg_3_p9, decodiicador7seg_3_p10, decodiicador7seg_3_p11
  // DECODIICADOR7SEG decodiicador7seg_4: pin names not known; wires that end beside it: main_4_p6, main_4_p5, main_4_p4, main_4_p3, decodiicador7seg_4_p5, decodiicador7seg_4_p6, decodiicador7seg_4_p7, decodiicador7seg_4_p8, decodiicador7seg_4_p9, decodiicador7seg_4_p10, decodiicador7seg_4_p11
  // DECODIICADOR7SEG decodiicador7seg_5: pin names not known; wires that end beside it: main_5_p6, main_5_p5, main_5_p4, main_5_p3, decodiicador7seg_5_p5, decodiicador7seg_5_p6, decodiicador7seg_5_p7, decodiicador7seg_5_p8, decodiicador7seg_5_p9, decodiicador7seg_5_p10, decodiicador7seg_5_p11
  _7_Segment_Display u_7_segment_display_2 (
    .g(decodiicador7seg_2_p11), .f(decodiicador7seg_2_p10), .a(decodiicador7seg_2_p5),
    .b(decodiicador7seg_2_p6), .e(decodiicador7seg_2_p9), .d(decodiicador7seg_2_p8), .c(decodiicador7seg_2_p7));  // open: dp
  _7_Segment_Display u_7_segment_display_3 (
    .g(decodiicador7seg_4_p11), .f(decodiicador7seg_4_p10), .a(decodiicador7seg_4_p5),
    .b(decodiicador7seg_4_p6), .e(decodiicador7seg_4_p9), .d(decodiicador7seg_4_p8), .c(decodiicador7seg_4_p7));  // open: dp
  // DECODIICADOR7SEG decodiicador7seg_6: pin names not known; wires that end beside it: main_6_p7, main_6_p6, main_6_p5, main_6_p4, decodiicador7seg_6_p5, decodiicador7seg_6_p6, decodiicador7seg_6_p7, decodiicador7seg_6_p8, decodiicador7seg_6_p9, decodiicador7seg_6_p10, decodiicador7seg_6_p11
  // DECODIICADOR7SEG decodiicador7seg_7: pin names not known; wires that end beside it: main_7_p6, main_7_p5, main_7_p4, main_7_p3, decodiicador7seg_7_p5, decodiicador7seg_7_p6, decodiicador7seg_7_p7, decodiicador7seg_7_p8, decodiicador7seg_7_p9, decodiicador7seg_7_p10, decodiicador7seg_7_p11
  _7_Segment_Display u_7_segment_display_4 (
    .g(decodiicador7seg_3_p11), .f(decodiicador7seg_3_p10), .a(decodiicador7seg_3_p5),
    .b(decodiicador7seg_3_p6), .e(decodiicador7seg_3_p9), .d(decodiicador7seg_3_p8), .c(decodiicador7seg_3_p7));  // open: dp
  _7_Segment_Display u_7_segment_display_5 (
    .g(decodiicador7seg_5_p11), .f(decodiicador7seg_5_p10), .a(decodiicador7seg_5_p5),
    .b(decodiicador7seg_5_p6), .e(decodiicador7seg_5_p9), .d(decodiicador7seg_5_p8), .c(decodiicador7seg_5_p7));  // open: dp
  _7_Segment_Display u_7_segment_display_6 (
    .g(decodiicador7seg_6_p11), .f(decodiicador7seg_6_p10), .a(decodiicador7seg_6_p5),
    .b(decodiicador7seg_6_p6), .e(decodiicador7seg_6_p9), .d(decodiicador7seg_6_p8), .c(decodiicador7seg_6_p7));  // open: dp
  _7_Segment_Display u_7_segment_display_7 (
    .g(decodiicador7seg_7_p11), .f(decodiicador7seg_7_p10), .a(decodiicador7seg_7_p5),
    .b(decodiicador7seg_7_p6), .e(decodiicador7seg_7_p9), .d(decodiicador7seg_7_p8), .c(decodiicador7seg_7_p7));  // open: dp
endmodule
